// Digital circuit LeTecMat4x4.dig as structural Verilog
module LeTecMat4x4 (
  input  clk,
  input  C0,
  input  C1,
  input  C2,
  input  C3,
  output Kp,
  output Q0,
  output Q1,
  output Q2,
  output Q3,
  output L0,
  output L1,
  output L2,
  output L3
);

  wire not_1_out, not_2_out;

  or or_1 (Q0, C1, C3);
  or or_2 (Q1, C2, C3);
  or or_3 (Kp, C3, C2, C1, C0);
  JK_FF jk_ff_1 (.J(1'b1), .C(clk), .K(1'b1), .Q(Q2));  // open: nQ
  and and_1 (L0, not_2_out, not_1_out);
  and and_2 (L1, not_2_out, Q2);
  and and_3 (L2, Q3, not_1_out);
  and and_4 (L3, Q3, Q2);
  not not_1 (not_1_out, Q2);
  JK_FF jk_ff_2 (.J(Q2), .C(clk), .K(Q2), .Q(Q3));  // open: nQ
  not not_2 (not_2_out, Q3);

  // Notes on the sheet:
  //   clk: Hz: 10
endmodule
